// Logisim project cpu.circ as structural Verilog: 1 circuit, main circuit cpu
module cpu (
  input  clk,
  input  [31:0] Instruction,
  input  [31:0] MemReadData,
  output [31:0] MemAddress,
  output [31:0] ProgramCounter,
  output [31:0] ra,
  output [31:0] sp,
  output [31:0] t0,
  output [31:0] t1,
  output [31:0] t2,
  output [31:0] s0,
  output [31:0] s1,
  output [31:0] a0,
  output [3:0] MemWriteMask,
  output [31:0] MemWriteData
);

  wire control_logic_1_asel, control_logic_1_bsel, control_logic_1_regwen;
  wire [3:0] control_logic_1_alusel;
  wire [31:0] adder_1_out, alu_1_aluresult, imm_gen_1_immediate, multiplexer_1_out, multiplexer_2_out,
       regfile_1_readdata1, regfile_1_readdata2;

  Register #(.width(32)) PC (.D(adder_1_out), .clk(clk), .Q(ProgramCounter));  // open: en, clr
  Adder #(.width(32)) adder_1 (.a(ProgramCounter), .b(32'h4), .out(adder_1_out));  // open: cin, cout
  imm_gen imm_gen_1 (.Instruction(Instruction), .Immediate(imm_gen_1_immediate));  // open: ImmSel
  control_logic control_logic_1 (
    .Instruction(Instruction), .RegWEn(control_logic_1_regwen), .ASel(control_logic_1_asel),
    .BSel(control_logic_1_bsel), .ALUSel(control_logic_1_alusel));  // open: BrEq, BrLt, PCSel, ImmSel, BrUn, MemRW, WBSel
  regfile regfile_1 (
    .ReadIndex1(Instruction[19:15]), .ReadIndex2(Instruction[24:20]), .WriteIndex(Instruction[11:7]),
    .WriteData(alu_1_aluresult), .RegWEn(control_logic_1_regwen), .clk(clk), .ra(ra), .sp(sp), .t0(t0),
    .t1(t1), .t2(t2), .s0(s0), .s1(s1), .a0(a0), .ReadData1(regfile_1_readdata1),
    .ReadData2(regfile_1_readdata2));
  Multiplexer #(.width(32)) multiplexer_1 (
    .in0(regfile_1_readdata1), .out(multiplexer_1_out), .sel(control_logic_1_asel));  // open: in1
  Multiplexer #(.width(32)) multiplexer_2 (
    .in0(regfile_1_readdata2), .in1(imm_gen_1_immediate), .out(multiplexer_2_out), .sel(control_logic_1_bsel));
  // partial_store partial_store_1: pin names not known
  // partial_load partial_load_1: pin names not known
  alu alu_1 (
    .A(multiplexer_1_out), .B(multiplexer_2_out), .ALUSel(control_logic_1_alusel), .ALUResult(alu_1_aluresult));
  // branch_comp branch_comp_1: pin names not known

  // Notes on the sheet:
  //   To IMEM
  //   IMEM (do **NOT** move this)
  //   From IMEM
  //   Inputs/Outputs for testing. Do **NOT** move these.
  //   To DMEM
  //   DMEM (do **NOT** move this)
  //   From DMEM
endmodule
